// Logisim project 74x161_163_194 .circ as structural Verilog: 3 circuits, main circuit 74x163
module _74x163 (
  input  CLK,
  input  CLR_L,
  input  LD_L,
  input  ENP,
  input  ENT,
  input  A,
  input  B,
  input  C,
  input  D,
  output QA,
  output QB,
  output QC,
  output QD,
  output RCO
);

  wire and_1_out, and_2_out, and_3_out, and_4_out, and_5_out, and_6_out, and_8_out, and_9_out, and_10_out,
       and_11_out, and_12_out, and_13_out, and_14_out, and_15_out, not_1_out, or_1_out, or_2_out, or_3_out,
       or_4_out, xor_1_out, xor_2_out, xor_3_out, xor_4_out;

  and and_1 (and_1_out, ENP, ENT);
  not not_1 (not_1_out, CLR_L);
  and and_2 (and_2_out, and_1_out, QA);
  and and_3 (and_3_out, and_1_out, QB, QA);
  and and_4 (and_4_out, and_1_out, QC, QB, QA);
  and and_5 (and_5_out, ~not_1_out, ~LD_L);  // AND_Gate
  and and_6 (and_6_out, ~and_5_out, ~not_1_out);  // AND_Gate
  xor xor_1 (xor_1_out, and_1_out, QA);
  xor xor_2 (xor_2_out, and_2_out, QB);
  xor xor_3 (xor_3_out, and_3_out, QC);
  xor xor_4 (xor_4_out, and_4_out, QD);
  and and_7 (RCO, QD, QC, QB, QA, ENT);
  and and_8 (and_8_out, and_5_out, A);
  and and_9 (and_9_out, and_6_out, xor_1_out);
  and and_10 (and_10_out, and_5_out, B);
  and and_11 (and_11_out, and_6_out, xor_2_out);
  and and_12 (and_12_out, and_5_out, C);
  and and_13 (and_13_out, and_6_out, xor_3_out);
  and and_14 (and_14_out, and_5_out, D);
  and and_15 (and_15_out, and_6_out, xor_4_out);
  or or_1 (or_1_out, and_8_out, and_9_out);
  or or_2 (or_2_out, and_10_out, and_11_out);
  or or_3 (or_3_out, and_12_out, and_13_out);
  or or_4 (or_4_out, and_14_out, and_15_out);
  D_Flip_Flop d_ff_1 (.clk(CLK), .D(or_1_out), .Q(QA));  // open: Qn, preset, en, reset
  D_Flip_Flop d_ff_2 (.clk(CLK), .D(or_2_out), .Q(QB));  // open: Qn, preset, en, reset
  D_Flip_Flop d_ff_3 (.clk(CLK), .D(or_3_out), .Q(QC));  // open: Qn, preset, en, reset
  D_Flip_Flop d_ff_4 (.clk(CLK), .D(or_4_out), .Q(QD));  // open: Qn, preset, en, reset

  // Notes on the sheet:
  //   Encapsulation made by Void Zero
  //   zero@smail.nju.edu.cn
endmodule

module _74x161 (
  input  CLK,
  input  CLR_L,
  input  LD_L,
  input  ENP,
  input  ENT,
  input  A,
  input  B,
  input  C,
  input  D,
  output QA,
  output QB,
  output QC,
  output QD,
  output RCO
);

  wire and_1_out, and_2_out, and_3_out, and_4_out, and_5_out, and_6_out, and_8_out, and_9_out, and_10_out,
       and_11_out, and_12_out, and_13_out, and_14_out, and_15_out, not_1_out, not_2_out, not_3_out,
       not_4_out, not_5_out, or_1_out, or_2_out, or_3_out, or_4_out, xor_1_out, xor_2_out, xor_3_out,
       xor_4_out;

  and and_1 (and_1_out, ENP, ENT);
  not not_1 (not_1_out, CLR_L);
  and and_2 (and_2_out, and_1_out, QA);
  and and_3 (and_3_out, and_1_out, QB, QA);
  and and_4 (and_4_out, and_1_out, QC, QB, QA);
  and and_5 (and_5_out, ~not_1_out, ~LD_L);  // AND_Gate
  and and_6 (and_6_out, ~and_5_out, ~not_1_out);  // AND_Gate
  xor xor_1 (xor_1_out, and_1_out, QA);
  xor xor_2 (xor_2_out, and_2_out, QB);
  xor xor_3 (xor_3_out, and_3_out, QC);
  xor xor_4 (xor_4_out, and_4_out, QD);
  and and_7 (RCO, QD, QC, QB, QA, ENT);
  and and_8 (and_8_out, and_5_out, A);
  and and_9 (and_9_out, and_6_out, xor_1_out);
  and and_10 (and_10_out, and_5_out, B);
  and and_11 (and_11_out, and_6_out, xor_2_out);
  and and_12 (and_12_out, and_5_out, C);
  and and_13 (and_13_out, and_6_out, xor_3_out);
  and and_14 (and_14_out, and_5_out, D);
  and and_15 (and_15_out, and_6_out, xor_4_out);
  or or_1 (or_1_out, and_8_out, and_9_out);
  or or_2 (or_2_out, and_10_out, and_11_out);
  or or_3 (or_3_out, and_12_out, and_13_out);
  or or_4 (or_4_out, and_14_out, and_15_out);
  D_Flip_Flop d_ff_1 (.clk(CLK), .D(or_1_out), .Q(QA), .reset(not_2_out));  // open: Qn, preset, en
  not not_2 (not_2_out, and_6_out);
  D_Flip_Flop d_ff_2 (.clk(CLK), .D(or_2_out), .Q(QB), .reset(not_3_out));  // open: Qn, preset, en
  not not_3 (not_3_out, and_6_out);
  D_Flip_Flop d_ff_3 (.clk(CLK), .D(or_3_out), .Q(QC), .reset(not_4_out));  // open: Qn, preset, en
  not not_4 (not_4_out, and_6_out);
  D_Flip_Flop d_ff_4 (.clk(CLK), .D(or_4_out), .Q(QD), .reset(not_5_out));  // open: Qn, preset, en
  not not_5 (not_5_out, and_6_out);

  // Notes on the sheet:
  //   Encapsulation made by Void Zero
  //   zero@smail.nju.edu.cn
endmodule

module _74x194 (
  input  CLK,
  input  CLR_L,
  input  S1,
  input  S0,
  input  LIN,
  input  D,
  input  C,
  input  B,
  input  A,
  input  RIN,
  output QD,
  output QC,
  output QB,
  output QA
);

  wire and_1_out, and_2_out, and_3_out, and_4_out, and_5_out, and_6_out, and_7_out, and_8_out, and_9_out,
       and_10_out, and_11_out, and_12_out, and_13_out, and_14_out, and_15_out, and_16_out, not_1_out,
       not_2_out, not_3_out, not_4_out, not_5_out, or_1_out, or_2_out, or_3_out, or_4_out;

  not not_1 (not_1_out, CLR_L);
  not not_2 (not_2_out, S1);
  not not_3 (not_3_out, S0);
  not not_4 (not_4_out, not_2_out);
  not not_5 (not_5_out, not_3_out);
  and and_1 (and_1_out, not_4_out, not_3_out, LIN);
  and and_2 (and_2_out, not_2_out, not_3_out, QD);
  and and_3 (and_3_out, not_4_out, not_5_out, D);
  and and_4 (and_4_out, not_2_out, not_5_out, QC);
  and and_5 (and_5_out, QD, not_4_out, not_3_out);
  and and_6 (and_6_out, not_2_out, not_3_out, QC);
  and and_7 (and_7_out, not_4_out, not_5_out, C);
  and and_8 (and_8_out, not_2_out, not_5_out, QB);
  and and_9 (and_9_out, QC, not_4_out, not_3_out);
  and and_10 (and_10_out, not_2_out, not_3_out, QB);
  and and_11 (and_11_out, not_4_out, not_5_out, B);
  and and_12 (and_12_out, not_2_out, not_5_out, QA);
  and and_13 (and_13_out, QB, not_4_out, not_3_out);
  and and_14 (and_14_out, QA, not_2_out, not_3_out);
  and and_15 (and_15_out, not_4_out, not_5_out, A);
  and and_16 (and_16_out, not_2_out, not_5_out, RIN);
  or or_1 (or_1_out, and_1_out, and_2_out, and_3_out, and_4_out);
  or or_2 (or_2_out, and_5_out, and_6_out, and_7_out, and_8_out);
  or or_3 (or_3_out, and_9_out, and_10_out, and_11_out, and_12_out);
  or or_4 (or_4_out, and_13_out, and_14_out, and_15_out, and_16_out);
  D_Flip_Flop d_ff_1 (.clk(CLK), .D(or_1_out), .Q(QD), .reset(not_1_out));  // open: Qn, preset, en
  D_Flip_Flop d_ff_2 (.clk(CLK), .D(or_2_out), .Q(QC), .reset(not_1_out));  // open: Qn, preset, en
  D_Flip_Flop d_ff_3 (.clk(CLK), .D(or_3_out), .Q(QB), .reset(not_1_out));  // open: Qn, preset, en
  D_Flip_Flop d_ff_4 (.clk(CLK), .D(or_4_out), .Q(QA), .reset(not_1_out));  // open: Qn, preset, en

  // Notes on the sheet:
  //   Encapsulation made by Void Zero
  //   zero@smail.nju.edu.cn
endmodule
