// Logisim project 74x194.circ as structural Verilog: 1 circuit, main circuit main
module main (
  input  CLK,
  input  CLR_L,
  input  S1,
  input  S0,
  input  LIN,
  input  D,
  input  C,
  input  B,
  input  A,
  input  RIN,
  output QD,
  output QC,
  output QB,
  output QA
);

  wire and_1_out, and_2_out, and_3_out, and_4_out, and_5_out, and_6_out, and_7_out, and_8_out, and_9_out,
       and_10_out, and_11_out, and_12_out, and_13_out, and_14_out, and_15_out, and_16_out, not_1_out,
       not_2_out, not_3_out, not_4_out, not_5_out, or_1_out, or_2_out, or_3_out, or_4_out, undriven;

  not not_1 (not_1_out, S1);
  not not_2 (not_2_out, S0);
  not not_3 (not_3_out, CLR_L);
  not not_4 (not_4_out, not_1_out);
  not not_5 (not_5_out, not_2_out);
  and and_1 (and_1_out, LIN, not_4_out, not_2_out);
  and and_2 (and_2_out, QD, not_1_out, not_2_out);
  and and_3 (and_3_out, D, not_4_out, not_5_out);
  and and_4 (and_4_out, QC, not_1_out, not_5_out);
  and and_5 (and_5_out, QD, not_4_out, not_2_out);
  and and_6 (and_6_out, QC, not_1_out, not_2_out);
  and and_7 (and_7_out, C, not_4_out, not_5_out);
  and and_8 (and_8_out, QB, not_1_out, not_5_out);
  and and_9 (and_9_out, QC, not_4_out, not_2_out);
  and and_10 (and_10_out, QB, not_1_out, not_2_out);
  and and_11 (and_11_out, B, not_4_out, not_5_out);
  and and_12 (and_12_out, QA, not_1_out, not_5_out);
  and and_13 (and_13_out, QB, not_4_out, not_2_out);
  and and_14 (and_14_out, QA, not_1_out, not_2_out);
  and and_15 (and_15_out, A, not_4_out, not_5_out);
  and and_16 (and_16_out, RIN, not_1_out, not_5_out);
  or or_1 (or_1_out, and_1_out, and_2_out, and_3_out, and_4_out);
  or or_2 (or_2_out, and_5_out, and_6_out, and_7_out, and_8_out);
  or or_3 (or_3_out, and_9_out, and_10_out, and_11_out, and_12_out);
  or or_4 (or_4_out, and_13_out, and_14_out, and_15_out, and_16_out);
  D_Flip_Flop d_ff_1 (.clk(CLK), .D(or_1_out), .Q(QD), .en(undriven), .reset(not_3_out));  // open: Qn, preset
  D_Flip_Flop d_ff_2 (.clk(CLK), .D(or_2_out), .Q(QC), .en(undriven), .reset(not_3_out));  // open: Qn, preset
  D_Flip_Flop d_ff_3 (.clk(CLK), .D(or_3_out), .Q(QB), .en(undriven), .reset(not_3_out));  // open: Qn, preset
  D_Flip_Flop d_ff_4 (.clk(CLK), .D(or_4_out), .Q(QA), .en(undriven), .reset(not_3_out));  // open: Qn, preset
endmodule
